# Fritzing sketch rfm95w-pico (saved by Fritzing 0.9.10b)
breadboards: 1

parts:
  Pico = Raspberry Pi Pico
  Adafruit_RFM95W = Adafruit RFM9x LoRa Radio
  RJ12_(To_meter) = RJ11 Jack [package=rj11-6]

nets:
  N1: Pico.pin_4, Adafruit_RFM95W.SCK
  N2: Pico.pin_5, Adafruit_RFM95W.MOSI
  N3: Pico.pin_6, Adafruit_RFM95W.MISO
  N4: Pico.pin_7, Adafruit_RFM95W.CS
  N5: Pico.pin_9, Adafruit_RFM95W.DIO0
  N6: Pico.pin_10, Adafruit_RFM95W.RST
  N7: Adafruit_RFM95W.VIN, RJ12_(To_meter).1
  N8: Adafruit_RFM95W.GND, RJ12_(To_meter).6

custom parts:
  Raspberry Pi Pico: Raspberry Pi Pico. Based around the RP2040 microcontroller the Pico is a low cost microcontroller device bringing Raspberry Pi quality, cost, and easy of use to the microcontroller space. Jan 2021, Split part in to two versions: tht (this one) and SMD. This one will drill holes for a .1 in header in pcb to allow plugging in the module as well as providing pads to solder the module to the top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
  Adafruit RFM9x LoRa Radio: Sending data over long distances is like magic, and now you can be a magician with this range of powerful and easy-to-use radio modules. Sure, sometimes you want to talk to a computer (a good time to use WiFi) or perhaps communicate with a Phone (choose Bluetooth Low Energy!) but what if you want to send data very far? Most WiFi, Bluetooth, Zigbee and other wireless chipsets use 2.4GHz, which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
