# Fritzing sketch rfm95w-rpi-4b (saved by Fritzing 0.9.10b)
breadboards: 1

parts:
  Adafruit_RFM95W = Adafruit RFM9x LoRa Radio
  Mod1 = Raspberry Pi 4B

nets:
  VIN: Adafruit_RFM95W.VIN, Mod1.5V
  GND: Adafruit_RFM95W.GND, Mod1.GND
  N1: Adafruit_RFM95W.DIO0, Mod1.GPIO17
  N2: Adafruit_RFM95W.SCK, Mod1.GPIO11
  N3: Adafruit_RFM95W.MISO, Mod1.GPIO9
  N4: Adafruit_RFM95W.MOSI, Mod1.GPIO10
  N5: Adafruit_RFM95W.CS, Mod1.GPIO8

custom parts:
  Adafruit RFM9x LoRa Radio: Sending data over long distances is like magic, and now you can be a magician with this range of powerful and easy-to-use radio modules. Sure, sometimes you want to talk to a computer (a good time to use WiFi) or perhaps communicate with a Phone (choose Bluetooth Low Energy!) but what if you want to send data very far? Most WiFi, Bluetooth, Zigbee and other wireless chipsets use 2.4GHz, which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
