# Fritzing sketch rj12-pico (saved by Fritzing 0.9.10b)
breadboards: 1

parts:
  Pico = Raspberry Pi Pico
  RJ12_(To_meter) = RJ11 Jack [package=rj11-6]
  BS170 = MOSFET-NCHANNEL [package=to220v]
  R1 = Resistor [tolerance=±1% resistance=10k package="1206 [SMD]"]
  R2 = Resistor [tolerance=±1% resistance=10k package="1206 [SMD]"]
  R3 = Resistor [tolerance=±1% resistance=220 package="1206 [SMD]"]

nets:
  N1: Pico.pin_2, BS170.D, R2.Pin_1
  N2: Pico.pin_3, Pico.pin_23, RJ12_(To_meter).3, RJ12_(To_meter).6, BS170.S
  N3: Pico.pin_36, R2.Pin_0
  N4: RJ12_(To_meter).1, R3.Pin_0
  N5: RJ12_(To_meter).2, R3.Pin_1
  N6: RJ12_(To_meter).5, BS170.G, R1.Pin_0

custom parts:
  Raspberry Pi Pico: Raspberry Pi Pico. Based around the RP2040 microcontroller the Pico is a low cost microcontroller device bringing Raspberry Pi quality, cost, and easy of use to the microcontroller space. Jan 2021, Split part in to two versions: tht (this one) and SMD. This one will drill holes for a .1 in header in pcb to allow plugging in the module as well as providing pads to solder the module to the top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
