# Fritzing sketch sd-pico (saved by Fritzing 0.9.10b)
breadboards: 1

parts:
  Pico = Raspberry Pi Pico
  RJ12_(To_meter) = RJ11 Jack [package=rj11-6]
  SD_Breakout = Adafruit MicroSD card breakout board [part_number="Adafruit #254"]

nets:
  N1: Pico.pin_14, SD_Breakout.CLK
  N2: Pico.pin_15, SD_Breakout.DO
  N3: Pico.pin_16, SD_Breakout.DI
  N4: Pico.pin_17, SD_Breakout.CS
  N5: RJ12_(To_meter).1, SD_Breakout.VCC
  N6: RJ12_(To_meter).6, SD_Breakout.GND

custom parts:
  Raspberry Pi Pico: Raspberry Pi Pico. Based around the RP2040 microcontroller the Pico is a low cost microcontroller device bringing Raspberry Pi quality, cost, and easy of use to the microcontroller space. Jan 2021, Split part in to two versions: tht (this one) and SMD. This one will drill holes for a .1 in header in pcb to allow plugging in the module as well as providing pads to solder the module to the top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
  Adafruit MicroSD card breakout board: Not just a simple breakout board, this microSD adapter goes the extra mile - designed for ease of use. Onboard 5v->3v regulator provides 150mA for power-hungry cards 3v level shifting means you can use this with ease on either 3v or 5v systems Uses a proper level shifting chip, not resistors: less problems, and faster read/write access Use 3 or 4 digital pins to read and write 2Gb+ of storage!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
